// Logisim project cpu.circ as structural Verilog: 12 circuits, main circuit main
module main (
  input  reset
);

  wire alu_1_zero, and_1_out, and_2_out, clk_out, instructcontrol_1_addorsub1, instructcontrol_1_aluinb1,
       instructcontrol_1_aluinb2, instructcontrol_1_arewebranching, instructcontrol_1_bleorbne,
       instructcontrol_1_inputdata1, instructcontrol_1_jalreg7, instructcontrol_1_jalstorepcplusone,
       instructcontrol_1_lwiregwritedatachoose, instructcontrol_1_memwriteenable,
       instructcontrol_1_readenablekb, instructcontrol_1_regwriteenable, instructcontrol_1_setoneforble,
       instructcontrol_1_setoneforbne, instructcontrol_1_setoneforj, instructcontrol_1_setoneforjr,
       instructcontrol_1_tordasdest, instructcontrol_1_writeenabletty, keyboard_1_avail,
       memory_latch_1_oe_latched, memory_latch_1_we_latched, multiplexer_8_out, not_1_out, not_2_out,
       not_3_out, or_1_out, xor_1_out, xor_2_out;
  wire [2:0] instructcontrol_1_aluop2, InstructMem_data_2, InstructMem_data_3, InstructMem_data_4,
       InstructMem_data_5, multiplexer_2_out, multiplexer_3_out;
  wire [3:0] InstructMem_data;
  wire [6:0] bit_extender_6_out, keyboard_1_data;
  wire [15:0] addersubtractor_1_s, alu_1_q, bit_extender_1_out, bit_extender_2_out, bit_extender_3_out,
       bit_extender_4_out, bit_extender_5_out, memory_latch_1_address_latched,
       memory_latch_1_data_in_latched, multiplexer_1_out, multiplexer_4_out, multiplexer_5_out,
       multiplexer_6_out, multiplexer_7_out, multiplexer_9_out, multiplexer_10_out, multiplexer_11_out,
       multiplexer_12_out, pc_1_q, plus1_1_aplus1, ram_1_dout, registerfile_1_readdata1,
       registerfile_1_readdata2;

  not not_1 (not_1_out, clk_out);
  not not_2 (not_2_out, clk_out);
  Keyboard keyboard_1 (
    .clk(not_2_out), .re(instructcontrol_1_readenablekb), .clr(reset), .avail(keyboard_1_avail),
    .data(keyboard_1_data));
  assign bit_extender_1_out = {{9{1'b0}}, keyboard_1_data};  // Bit_Extender bit_extender_1
  pc pc_1 (.Reset(reset), .clk(not_1_out), .Enable(1'b1), .D(multiplexer_11_out), .Q(pc_1_q));
  ROM #(.addrWidth(16), .dataWidth(16)) InstructMem (
    .addr(pc_1_q),
    .data({InstructMem_data, InstructMem_data_5, InstructMem_data_4, InstructMem_data_3, InstructMem_data_2}));
  assign bit_extender_2_out = {{15{1'b0}}, keyboard_1_avail};  // Bit_Extender bit_extender_2
  plus1 plus1_1 (.a(pc_1_q), .aplus1(plus1_1_aplus1));  // open: cout
  xor xor_1 (xor_1_out, keyboard_1_avail, instructcontrol_1_inputdata1);
  Multiplexer #(.width(16), .enable("false")) multiplexer_1 (
    .in0(bit_extender_1_out), .in1(bit_extender_2_out), .out(multiplexer_1_out), .sel(xor_1_out));
  instructcontrol instructcontrol_1 (
    .in_1(InstructMem_data), .ALUop0(instructcontrol_1_aluop2[2]), .ALUop1(instructcontrol_1_aluop2[1]),
    .ALUop2(instructcontrol_1_aluop2[0]), .ReadEnableKB(instructcontrol_1_readenablekb),
    .INPUTDATA1(instructcontrol_1_inputdata1), .WriteEnableTTY(instructcontrol_1_writeenabletty),
    .TorDasDest(instructcontrol_1_tordasdest), .RegWriteEnable(instructcontrol_1_regwriteenable),
    .MemWriteEnable(instructcontrol_1_memwriteenable),
    .LWIRegWriteDataChoose(instructcontrol_1_lwiregwritedatachoose),
    .SetOneForJR(instructcontrol_1_setoneforjr), .SetOneForJ(instructcontrol_1_setoneforj),
    .SetOneForBLE(instructcontrol_1_setoneforble), .SetOneForBNE(instructcontrol_1_setoneforbne),
    .BLEorBNE(instructcontrol_1_bleorbne), .JALReg7(instructcontrol_1_jalreg7),
    .ALUinB1(instructcontrol_1_aluinb1), .ALUinB2(instructcontrol_1_aluinb2),
    .JALSTOREPCPLUSONE(instructcontrol_1_jalstorepcplusone), .AddOrSub1(instructcontrol_1_addorsub1),
    .AreWeBranching(instructcontrol_1_arewebranching));
  Multiplexer #(.width(3), .enable("false")) multiplexer_2 (
    .in0(multiplexer_3_out), .in1(3'b111), .out(multiplexer_2_out), .sel(instructcontrol_1_jalreg7));
  Multiplexer #(.width(3), .enable("false")) multiplexer_3 (
    .in0(InstructMem_data_4), .in1(InstructMem_data_3), .out(multiplexer_3_out),
    .sel(instructcontrol_1_tordasdest));
  Multiplexer #(.width(16), .enable("false")) multiplexer_4 (
    .in0(multiplexer_12_out), .in1(plus1_1_aplus1), .out(multiplexer_4_out),
    .sel(instructcontrol_1_jalstorepcplusone));
  Multiplexer #(.width(16), .enable("false")) multiplexer_5 (
    .in0(multiplexer_4_out), .in1(multiplexer_1_out), .out(multiplexer_5_out),
    .sel(instructcontrol_1_inputdata1));
  Clock clk (.out(clk_out));
  assign bit_extender_3_out = {{10{InstructMem_data_3[2]}}, {InstructMem_data_3, InstructMem_data_2}};  // Bit_Extender bit_extender_3
  assign bit_extender_4_out = {{4{1'b0}}, {InstructMem_data_5, InstructMem_data_4, InstructMem_data_3, InstructMem_data_2}};  // Bit_Extender bit_extender_4
  RegisterFile registerfile_1 (
    .WriteData(multiplexer_5_out), .reset(reset), .WriteReg(multiplexer_2_out),
    .RegWriteEnable(instructcontrol_1_regwriteenable), .clk(clk_out), .ReadReg2(InstructMem_data_4),
    .ReadReg1(InstructMem_data_5), .ReadData1(registerfile_1_readdata1), .ReadData2(registerfile_1_readdata2));
  assign bit_extender_5_out = {{13{1'b0}}, InstructMem_data_2};  // Bit_Extender bit_extender_5
  Multiplexer #(.width(16), .enable("false")) multiplexer_6 (
    .in0(registerfile_1_readdata2), .in1(bit_extender_3_out), .out(multiplexer_6_out),
    .sel(instructcontrol_1_aluinb1));
  Multiplexer #(.width(16), .enable("false")) multiplexer_7 (
    .in0(multiplexer_6_out), .in1(bit_extender_5_out), .out(multiplexer_7_out),
    .sel(instructcontrol_1_aluinb2));
  addersubtractor addersubtractor_1 (
    .a(plus1_1_aplus1), .b(bit_extender_3_out), .addsub(1'b0), .s(addersubtractor_1_s));  // open: cout
  and and_1 (and_1_out, instructcontrol_1_setoneforble, alu_1_q[15]);
  or or_1 (or_1_out, alu_1_zero, and_1_out);
  ALU alu_1 (
    .a(registerfile_1_readdata1), .b(multiplexer_7_out), .Selection(instructcontrol_1_aluop2),
    .addsub(instructcontrol_1_addorsub1), .ZERO(alu_1_zero), .Q(alu_1_q));  // open: cout
  xor xor_2 (xor_2_out, instructcontrol_1_setoneforbne, alu_1_zero);
  and and_2 (and_2_out, instructcontrol_1_arewebranching, multiplexer_8_out);
  Multiplexer #(.enable("false")) multiplexer_8 (
    .in0(or_1_out), .in1(xor_2_out), .out(multiplexer_8_out), .sel(instructcontrol_1_bleorbne));
  Multiplexer #(.width(16), .enable("false")) multiplexer_9 (
    .in0(plus1_1_aplus1), .in1(addersubtractor_1_s), .out(multiplexer_9_out), .sel(and_2_out));
  not not_3 (not_3_out, clk_out);
  Multiplexer #(.width(16), .enable("false")) multiplexer_10 (
    .in0(multiplexer_9_out), .in1(bit_extender_4_out), .out(multiplexer_10_out),
    .sel(instructcontrol_1_setoneforj));
  Multiplexer #(.width(16), .enable("false")) multiplexer_11 (
    .in0(multiplexer_10_out), .in1(registerfile_1_readdata1), .out(multiplexer_11_out),
    .sel(instructcontrol_1_setoneforjr));
  Bit_Extender #(.in_width(16), .out_width(7)) bit_extender_6 (.in(registerfile_1_readdata1), .out(bit_extender_6_out));
  RAM #(.addrWidth(16), .dataWidth(16), .trigger("high"), .databus("bibus")) ram_1 (
    .addr(memory_latch_1_address_latched), .we(memory_latch_1_we_latched), .oe(memory_latch_1_oe_latched),
    .din(memory_latch_1_data_in_latched), .dout(ram_1_dout));
  memory_latch memory_latch_1 (
    .address(alu_1_q), .WE(instructcontrol_1_memwriteenable), .clk(not_3_out),
    .data_in(registerfile_1_readdata2), .address_latched(memory_latch_1_address_latched),
    .WE_latched(memory_latch_1_we_latched), .OE_latched(memory_latch_1_oe_latched),
    .data_in_latched(memory_latch_1_data_in_latched));
  TTY #(.rows(13), .cols(80)) tty_1 (
    .data(bit_extender_6_out), .clk(clk_out), .we(instructcontrol_1_writeenabletty), .clr(reset));
  Multiplexer #(.width(16), .enable("false")) multiplexer_12 (
    .in0(alu_1_q), .in1(ram_1_dout), .out(multiplexer_12_out), .sel(instructcontrol_1_lwiregwritedatachoose));
endmodule

module sxtnbitreg (
  input  Reset,
  input  clk,
  input  Enable,
  input  [15:0] D,
  output [15:0] Q
);

  wire and_1_out;

  and and_1 (and_1_out, clk, Enable);
  D_Flip_Flop d_ff_1 (.D(D[0]), .clk(and_1_out), .Q(Q[0]), .reset(Reset));  // open: Qn, preset
  D_Flip_Flop d_ff_2 (.D(D[1]), .clk(and_1_out), .Q(Q[1]));  // open: Qn, preset, reset
  D_Flip_Flop d_ff_3 (.D(D[2]), .clk(and_1_out), .Q(Q[2]), .reset(Reset));  // open: Qn, preset
  D_Flip_Flop d_ff_4 (.D(D[3]), .clk(and_1_out), .Q(Q[3]), .reset(Reset));  // open: Qn, preset
  D_Flip_Flop d_ff_5 (.D(D[4]), .clk(and_1_out), .Q(Q[4]), .reset(Reset));  // open: Qn, preset
  D_Flip_Flop d_ff_6 (.D(D[5]), .clk(and_1_out), .Q(Q[5]), .reset(Reset));  // open: Qn, preset
  D_Flip_Flop d_ff_7 (.D(D[6]), .clk(and_1_out), .Q(Q[6]), .reset(Reset));  // open: Qn, preset
  D_Flip_Flop d_ff_8 (.D(D[7]), .clk(and_1_out), .Q(Q[7]), .reset(Reset));  // open: Qn, preset
  D_Flip_Flop d_ff_9 (.D(D[8]), .clk(and_1_out), .Q(Q[8]), .reset(Reset));  // open: Qn, preset
  D_Flip_Flop d_ff_10 (.D(D[9]), .clk(and_1_out), .Q(Q[9]), .reset(Reset));  // open: Qn, preset
  D_Flip_Flop d_ff_11 (.D(D[10]), .clk(and_1_out), .Q(Q[10]), .reset(Reset));  // open: Qn, preset
  D_Flip_Flop d_ff_12 (.D(D[11]), .clk(and_1_out), .Q(Q[11]), .reset(Reset));  // open: Qn, preset
  D_Flip_Flop d_ff_13 (.D(D[12]), .clk(and_1_out), .Q(Q[12]), .reset(Reset));  // open: Qn, preset
  D_Flip_Flop d_ff_14 (.D(D[13]), .clk(and_1_out), .Q(Q[13]), .reset(Reset));  // open: Qn, preset
  D_Flip_Flop d_ff_15 (.D(D[14]), .clk(and_1_out), .Q(Q[14]), .reset(Reset));  // open: Qn, preset
  D_Flip_Flop d_ff_16 (.D(D[15]), .clk(and_1_out), .Q(Q[15]), .reset(Reset));  // open: Qn, preset
endmodule

module RegisterFile (
  input  [15:0] WriteData,
  input  reset,
  input  [2:0] WriteReg,
  input  RegWriteEnable,
  input  clk,
  input  [2:0] ReadReg2,
  input  [2:0] ReadReg1,
  output [15:0] ReadData1,
  output [15:0] ReadData2
);

  wire and_1_out, and_2_out, and_3_out, and_4_out, and_5_out, and_6_out, and_7_out, decoder_1_out1,
       decoder_1_out2, decoder_1_out3, decoder_1_out4, decoder_1_out5, decoder_1_out6, decoder_1_out7,
       decoder_2_out0, decoder_2_out1, decoder_2_out2, decoder_2_out3, decoder_2_out4, decoder_2_out5,
       decoder_2_out6, decoder_2_out7, decoder_3_out0, decoder_3_out1, decoder_3_out2, decoder_3_out3,
       decoder_3_out4, decoder_3_out5, decoder_3_out6, decoder_3_out7;
  wire [15:0] reg1_q, reg2_q, reg3_q, reg4_q, reg5_q, reg6_q, reg7_q;

  Decoder #(.select(3)) decoder_1 (
    .out1(decoder_1_out1), .out2(decoder_1_out2), .out3(decoder_1_out3), .out4(decoder_1_out4),
    .out5(decoder_1_out5), .out6(decoder_1_out6), .out7(decoder_1_out7), .sel(WriteReg));  // open: out0, en
  and and_1 (and_1_out, decoder_1_out1, RegWriteEnable);
  and and_2 (and_2_out, decoder_1_out2, RegWriteEnable);
  and and_3 (and_3_out, decoder_1_out3, RegWriteEnable);
  and and_4 (and_4_out, RegWriteEnable, decoder_1_out4);
  and and_5 (and_5_out, decoder_1_out5, RegWriteEnable);
  and and_6 (and_6_out, decoder_1_out6, RegWriteEnable);
  and and_7 (and_7_out, decoder_1_out7, RegWriteEnable);
  Decoder #(.select(3)) decoder_2 (
    .out0(decoder_2_out0), .out1(decoder_2_out1), .out2(decoder_2_out2), .out3(decoder_2_out3),
    .out4(decoder_2_out4), .out5(decoder_2_out5), .out6(decoder_2_out6), .out7(decoder_2_out7), .sel(ReadReg1));  // open: en
  Decoder #(.select(3)) decoder_3 (
    .out0(decoder_3_out0), .out1(decoder_3_out1), .out2(decoder_3_out2), .out3(decoder_3_out3),
    .out4(decoder_3_out4), .out5(decoder_3_out5), .out6(decoder_3_out6), .out7(decoder_3_out7), .sel(ReadReg2));  // open: en
  // Probe on {16{1'b0}}
  sxtnbitreg reg1 (.Reset(reset), .clk(clk), .Enable(and_1_out), .D(WriteData), .Q(reg1_q));
  sxtnbitreg reg2 (.Reset(reset), .clk(clk), .Enable(and_2_out), .D(WriteData), .Q(reg2_q));
  sxtnbitreg reg3 (.Reset(reset), .clk(clk), .Enable(and_3_out), .D(WriteData), .Q(reg3_q));
  sxtnbitreg reg4 (.Reset(reset), .clk(clk), .Enable(and_4_out), .D(WriteData), .Q(reg4_q));
  sxtnbitreg reg5 (.Reset(reset), .clk(clk), .Enable(and_5_out), .D(WriteData), .Q(reg5_q));
  sxtnbitreg reg6 (.Reset(reset), .clk(clk), .Enable(and_6_out), .D(WriteData), .Q(reg6_q));
  sxtnbitreg reg7 (.Reset(reset), .clk(clk), .Enable(and_7_out), .D(WriteData), .Q(reg7_q));
  // Probe on reg1_q
  // Probe on reg2_q
  // Probe on reg3_q
  // Probe on reg4_q
  // Probe on reg5_q
  // Probe on reg6_q
  // Probe on reg7_q
  assign ReadData2 = decoder_3_out0 ? {16{1'b0}} : 16'bz;  // Controlled_Buffer controlled_buffer_1
  assign ReadData2 = decoder_3_out1 ? reg1_q : 16'bz;  // Controlled_Buffer controlled_buffer_2
  assign ReadData2 = decoder_3_out2 ? reg2_q : 16'bz;  // Controlled_Buffer controlled_buffer_3
  assign ReadData2 = decoder_3_out3 ? reg3_q : 16'bz;  // Controlled_Buffer controlled_buffer_4
  assign ReadData2 = decoder_3_out4 ? reg4_q : 16'bz;  // Controlled_Buffer controlled_buffer_5
  assign ReadData2 = decoder_3_out5 ? reg5_q : 16'bz;  // Controlled_Buffer controlled_buffer_6
  assign ReadData2 = decoder_3_out6 ? reg6_q : 16'bz;  // Controlled_Buffer controlled_buffer_7
  assign ReadData2 = decoder_3_out7 ? reg7_q : 16'bz;  // Controlled_Buffer controlled_buffer_8
  assign ReadData1 = decoder_2_out0 ? {16{1'b0}} : 16'bz;  // Controlled_Buffer controlled_buffer_9
  assign ReadData1 = decoder_2_out1 ? reg1_q : 16'bz;  // Controlled_Buffer controlled_buffer_10
  assign ReadData1 = decoder_2_out2 ? reg2_q : 16'bz;  // Controlled_Buffer controlled_buffer_11
  assign ReadData1 = decoder_2_out3 ? reg3_q : 16'bz;  // Controlled_Buffer controlled_buffer_12
  assign ReadData1 = decoder_2_out4 ? reg4_q : 16'bz;  // Controlled_Buffer controlled_buffer_13
  assign ReadData1 = decoder_2_out5 ? reg5_q : 16'bz;  // Controlled_Buffer controlled_buffer_14
  assign ReadData1 = decoder_2_out6 ? reg6_q : 16'bz;  // Controlled_Buffer controlled_buffer_15
  assign ReadData1 = decoder_2_out7 ? reg7_q : 16'bz;  // Controlled_Buffer controlled_buffer_16
endmodule

module ALU (
  input  [15:0] a,
  input  [15:0] b,
  input  [2:0] Selection,
  input  addsub,
  output ZERO,
  output [15:0] Q,
  output cout
);

  wire or_2_out, or_3_out, or_4_out, or_5_out, or_6_out, or_7_out, or_8_out, or_9_out, or_10_out, or_11_out,
       or_12_out, or_13_out, or_14_out, or_15_out, or_16_out;
  wire [2:0] bit_extender_1_out;
  wire [15:0] addersubtractor_1_s, and_1_out, leftbitshifter_1_aftershift, not_1_out, or_1_out,
       rightbitshifter_1_aftershift;

  Bit_Extender #(.in_width(16), .out_width(3), .\type ("zero")) bit_extender_1 (.in(b), .out(bit_extender_1_out));
  assign not_1_out = ~a;  // NOT_Gate not_1, 16 bits wide
  assign and_1_out = a & b;  // AND_Gate and_1, 16 bits wide
  assign or_1_out = a | b;  // OR_Gate or_1, 16 bits wide
  leftbitshifter leftbitshifter_1 (
    .beforeshift(a), .shamt(bit_extender_1_out), .aftershift(leftbitshifter_1_aftershift));
  rightbitshifter rightbitshifter_1 (
    .beforeshift(a), .shamt(bit_extender_1_out), .aftershift(rightbitshifter_1_aftershift));
  addersubtractor addersubtractor_1 (.a(a), .b(b), .addsub(addsub), .s(addersubtractor_1_s), .cout(cout));
  Multiplexer #(.select(3), .width(16), .enable("false")) multiplexer_1 (
    .in0(leftbitshifter_1_aftershift), .in1(rightbitshifter_1_aftershift), .in2(and_1_out), .in3(or_1_out),
    .in4(not_1_out), .in5(addersubtractor_1_s), .out(Q), .sel(Selection));  // open: in6, in7
  or or_2 (or_2_out, Q[0], Q[1]);
  or or_3 (or_3_out, Q[2], Q[3]);
  or or_4 (or_4_out, Q[4], Q[5]);
  or or_5 (or_5_out, Q[6], Q[7]);
  or or_6 (or_6_out, Q[8], Q[9]);
  or or_7 (or_7_out, Q[10], Q[11]);
  or or_8 (or_8_out, Q[12], Q[13]);
  or or_9 (or_9_out, Q[14], Q[15]);
  or or_10 (or_10_out, or_2_out, or_3_out);
  or or_11 (or_11_out, or_4_out, or_5_out);
  or or_12 (or_12_out, or_6_out, or_7_out);
  or or_13 (or_13_out, or_8_out, or_9_out);
  or or_14 (or_14_out, or_10_out, or_11_out);
  or or_15 (or_15_out, or_12_out, or_13_out);
  or or_16 (or_16_out, or_14_out, or_15_out);
  not not_2 (ZERO, or_16_out);
endmodule

module addersubtractor (
  input  [15:0] a,
  input  [15:0] b,
  input  addsub,
  output [15:0] s,
  output cout
);

  wire onebitadder_1_cout, onebitadder_2_cout, onebitadder_3_cout, onebitadder_4_cout, onebitadder_5_cout,
       onebitadder_6_cout, onebitadder_7_cout, onebitadder_8_cout, onebitadder_9_cout, onebitadder_10_cout,
       onebitadder_11_cout, onebitadder_12_cout, onebitadder_13_cout, onebitadder_14_cout,
       onebitadder_15_cout, xor_1_out, xor_2_out, xor_3_out, xor_4_out, xor_5_out, xor_6_out, xor_7_out,
       xor_8_out, xor_9_out, xor_10_out, xor_11_out, xor_12_out, xor_13_out, xor_14_out, xor_15_out,
       xor_16_out;

  xor xor_1 (xor_1_out, b[0], addsub);
  onebitadder onebitadder_1 (.cin(addsub), .a(a[0]), .b(xor_1_out), .sum(s[0]), .cout(onebitadder_1_cout));
  xor xor_2 (xor_2_out, b[1], addsub);
  onebitadder onebitadder_2 (.cin(onebitadder_1_cout), .a(a[1]), .b(xor_2_out), .sum(s[1]), .cout(onebitadder_2_cout));
  xor xor_3 (xor_3_out, b[2], addsub);
  onebitadder onebitadder_3 (.cin(onebitadder_2_cout), .a(a[2]), .b(xor_3_out), .sum(s[2]), .cout(onebitadder_3_cout));
  xor xor_4 (xor_4_out, b[3], addsub);
  onebitadder onebitadder_4 (.cin(onebitadder_3_cout), .a(a[3]), .b(xor_4_out), .sum(s[3]), .cout(onebitadder_4_cout));
  xor xor_5 (xor_5_out, b[4], addsub);
  onebitadder onebitadder_5 (.cin(onebitadder_4_cout), .a(a[4]), .b(xor_5_out), .sum(s[4]), .cout(onebitadder_5_cout));
  xor xor_6 (xor_6_out, b[5], addsub);
  onebitadder onebitadder_6 (.cin(onebitadder_5_cout), .a(a[5]), .b(xor_6_out), .sum(s[5]), .cout(onebitadder_6_cout));
  xor xor_7 (xor_7_out, b[6], addsub);
  onebitadder onebitadder_7 (.cin(onebitadder_6_cout), .a(a[6]), .b(xor_7_out), .sum(s[6]), .cout(onebitadder_7_cout));
  xor xor_8 (xor_8_out, b[7], addsub);
  onebitadder onebitadder_8 (.cin(onebitadder_7_cout), .a(a[7]), .b(xor_8_out), .sum(s[7]), .cout(onebitadder_8_cout));
  xor xor_9 (xor_9_out, b[8], addsub);
  onebitadder onebitadder_9 (.cin(onebitadder_8_cout), .a(a[8]), .b(xor_9_out), .sum(s[8]), .cout(onebitadder_9_cout));
  xor xor_10 (xor_10_out, b[9], addsub);
  onebitadder onebitadder_10 (
    .cin(onebitadder_9_cout), .a(a[9]), .b(xor_10_out), .sum(s[9]), .cout(onebitadder_10_cout));
  xor xor_11 (xor_11_out, b[10], addsub);
  onebitadder onebitadder_11 (
    .cin(onebitadder_10_cout), .a(a[10]), .b(xor_11_out), .sum(s[10]), .cout(onebitadder_11_cout));
  xor xor_12 (xor_12_out, b[11], addsub);
  onebitadder onebitadder_12 (
    .cin(onebitadder_11_cout), .a(a[11]), .b(xor_12_out), .sum(s[11]), .cout(onebitadder_12_cout));
  xor xor_13 (xor_13_out, b[12], addsub);
  onebitadder onebitadder_13 (
    .cin(onebitadder_12_cout), .a(a[12]), .b(xor_13_out), .sum(s[12]), .cout(onebitadder_13_cout));
  xor xor_14 (xor_14_out, b[13], addsub);
  onebitadder onebitadder_14 (
    .cin(onebitadder_13_cout), .a(a[13]), .b(xor_14_out), .sum(s[13]), .cout(onebitadder_14_cout));
  xor xor_15 (xor_15_out, b[14], addsub);
  onebitadder onebitadder_15 (
    .cin(onebitadder_14_cout), .a(a[14]), .b(xor_15_out), .sum(s[14]), .cout(onebitadder_15_cout));
  xor xor_16 (xor_16_out, b[15], addsub);
  onebitadder onebitadder_16 (.cin(onebitadder_15_cout), .a(a[15]), .b(xor_16_out), .sum(s[15]), .cout(cout));
endmodule

module onebitadder (
  input  cin,
  input  a,
  input  b,
  output sum,
  output cout
);

  wire and_1_out, and_2_out, xor_1_out;

  and and_1 (and_1_out, b, a);
  or or_1 (cout, and_1_out, and_2_out);
  xor xor_1 (xor_1_out, a, b);
  and and_2 (and_2_out, xor_1_out, cin);
  xor xor_2 (sum, cin, xor_1_out);
endmodule

module pc (
  input  Reset,
  input  clk,
  input  Enable,
  input  [15:0] D,
  output [15:0] Q
);

  wire and_1_out;

  and and_1 (and_1_out, clk, Enable);
  D_Flip_Flop d_ff_1 (.D(D[0]), .clk(and_1_out), .Q(Q[0]), .reset(Reset));  // open: Qn, preset
  D_Flip_Flop d_ff_2 (.D(D[1]), .clk(and_1_out), .Q(Q[1]));  // open: Qn, preset, reset
  D_Flip_Flop d_ff_3 (.D(D[2]), .clk(and_1_out), .Q(Q[2]), .reset(Reset));  // open: Qn, preset
  D_Flip_Flop d_ff_4 (.D(D[3]), .clk(and_1_out), .Q(Q[3]), .reset(Reset));  // open: Qn, preset
  D_Flip_Flop d_ff_5 (.D(D[4]), .clk(and_1_out), .Q(Q[4]), .reset(Reset));  // open: Qn, preset
  D_Flip_Flop d_ff_6 (.D(D[5]), .clk(and_1_out), .Q(Q[5]), .reset(Reset));  // open: Qn, preset
  D_Flip_Flop d_ff_7 (.D(D[6]), .clk(and_1_out), .Q(Q[6]), .reset(Reset));  // open: Qn, preset
  D_Flip_Flop d_ff_8 (.D(D[7]), .clk(and_1_out), .Q(Q[7]), .reset(Reset));  // open: Qn, preset
  D_Flip_Flop d_ff_9 (.D(D[8]), .clk(and_1_out), .Q(Q[8]), .reset(Reset));  // open: Qn, preset
  D_Flip_Flop d_ff_10 (.D(D[9]), .clk(and_1_out), .Q(Q[9]), .reset(Reset));  // open: Qn, preset
  D_Flip_Flop d_ff_11 (.D(D[10]), .clk(and_1_out), .Q(Q[10]), .reset(Reset));  // open: Qn, preset
  D_Flip_Flop d_ff_12 (.D(D[11]), .clk(and_1_out), .Q(Q[11]), .reset(Reset));  // open: Qn, preset
  D_Flip_Flop d_ff_13 (.D(D[12]), .clk(and_1_out), .Q(Q[12]), .reset(Reset));  // open: Qn, preset
  D_Flip_Flop d_ff_14 (.D(D[13]), .clk(and_1_out), .Q(Q[13]), .reset(Reset));  // open: Qn, preset
  D_Flip_Flop d_ff_15 (.D(D[14]), .clk(and_1_out), .Q(Q[14]), .reset(Reset));  // open: Qn, preset
  D_Flip_Flop d_ff_16 (.D(D[15]), .clk(and_1_out), .Q(Q[15]), .reset(Reset));  // open: Qn, preset
endmodule

module plus1 (
  input  [15:0] a,
  output [15:0] aplus1,
  output cout
);

  wire onebitadder_1_cout, onebitadder_2_cout, onebitadder_3_cout, onebitadder_4_cout, onebitadder_5_cout,
       onebitadder_6_cout, onebitadder_7_cout, onebitadder_8_cout, onebitadder_9_cout, onebitadder_10_cout,
       onebitadder_11_cout, onebitadder_12_cout, onebitadder_13_cout, onebitadder_14_cout,
       onebitadder_15_cout;

  onebitadder onebitadder_1 (.cin(1'b0), .a(a[0]), .b(1'b1), .sum(aplus1[0]), .cout(onebitadder_1_cout));
  onebitadder onebitadder_2 (.cin(onebitadder_1_cout), .a(a[1]), .b(1'b0), .sum(aplus1[1]), .cout(onebitadder_2_cout));
  onebitadder onebitadder_3 (.cin(onebitadder_2_cout), .a(a[2]), .b(1'b0), .sum(aplus1[2]), .cout(onebitadder_3_cout));
  onebitadder onebitadder_4 (.cin(onebitadder_3_cout), .a(a[3]), .b(1'b0), .sum(aplus1[3]), .cout(onebitadder_4_cout));
  onebitadder onebitadder_5 (.cin(onebitadder_4_cout), .a(a[4]), .b(1'b0), .sum(aplus1[4]), .cout(onebitadder_5_cout));
  onebitadder onebitadder_6 (.cin(onebitadder_5_cout), .a(a[5]), .b(1'b0), .sum(aplus1[5]), .cout(onebitadder_6_cout));
  onebitadder onebitadder_7 (.cin(onebitadder_6_cout), .a(a[6]), .b(1'b0), .sum(aplus1[6]), .cout(onebitadder_7_cout));
  onebitadder onebitadder_8 (.cin(onebitadder_7_cout), .a(a[7]), .b(1'b0), .sum(aplus1[7]), .cout(onebitadder_8_cout));
  onebitadder onebitadder_9 (.cin(onebitadder_8_cout), .a(a[8]), .b(1'b0), .sum(aplus1[8]), .cout(onebitadder_9_cout));
  onebitadder onebitadder_10 (
    .cin(onebitadder_9_cout), .a(a[9]), .b(1'b0), .sum(aplus1[9]), .cout(onebitadder_10_cout));
  onebitadder onebitadder_11 (
    .cin(onebitadder_10_cout), .a(a[10]), .b(1'b0), .sum(aplus1[10]), .cout(onebitadder_11_cout));
  onebitadder onebitadder_12 (
    .cin(onebitadder_11_cout), .a(a[11]), .b(1'b0), .sum(aplus1[11]), .cout(onebitadder_12_cout));
  onebitadder onebitadder_13 (
    .cin(onebitadder_12_cout), .a(a[12]), .b(1'b0), .sum(aplus1[12]), .cout(onebitadder_13_cout));
  onebitadder onebitadder_14 (
    .cin(onebitadder_13_cout), .a(a[13]), .b(1'b0), .sum(aplus1[13]), .cout(onebitadder_14_cout));
  onebitadder onebitadder_15 (
    .cin(onebitadder_14_cout), .a(a[14]), .b(1'b0), .sum(aplus1[14]), .cout(onebitadder_15_cout));
  onebitadder onebitadder_16 (.cin(onebitadder_15_cout), .a(a[15]), .b(1'b0), .sum(aplus1[15]), .cout(cout));
endmodule

module instructcontrol (
  input  [3:0] in_1,
  output ALUop0,
  output ALUop1,
  output ALUop2,
  output ReadEnableKB,
  output INPUTDATA1,
  output WriteEnableTTY,
  output TorDasDest,
  output RegWriteEnable,
  output MemWriteEnable,
  output LWIRegWriteDataChoose,
  output SetOneForJR,
  output SetOneForJ,
  output SetOneForBLE,
  output SetOneForBNE,
  output BLEorBNE,
  output JALReg7,
  output ALUinB1,
  output ALUinB2,
  output JALSTOREPCPLUSONE,
  output AddOrSub1,
  output AreWeBranching
);

  wire decoder_1_out0, decoder_1_out1, decoder_1_out2, decoder_1_out3, decoder_1_out4, decoder_1_out6,
       decoder_1_out11;

  Decoder #(.select(4)) decoder_1 (
    .out0(decoder_1_out0), .out1(decoder_1_out1), .out2(decoder_1_out2), .out3(decoder_1_out3),
    .out4(decoder_1_out4), .out5(ALUop1), .out6(decoder_1_out6), .out7(LWIRegWriteDataChoose),
    .out8(MemWriteEnable), .out9(BLEorBNE), .out10(SetOneForBLE), .out11(decoder_1_out11),
    .out12(SetOneForJR), .out13(JALReg7), .out14(INPUTDATA1), .out15(WriteEnableTTY), .sel(in_1));  // open: en
  or or_1 (TorDasDest, ALUop1, ALUop1, decoder_1_out4, decoder_1_out6, decoder_1_out3, decoder_1_out2, decoder_1_out0);
  or or_2 (RegWriteEnable, INPUTDATA1, ALUop1, decoder_1_out1, decoder_1_out2, decoder_1_out4, decoder_1_out3, decoder_1_out0, decoder_1_out6, LWIRegWriteDataChoose, JALReg7);
  or or_3 (ALUinB1, MemWriteEnable, LWIRegWriteDataChoose, decoder_1_out1);
  or or_4 (ALUinB2, decoder_1_out4, decoder_1_out3);
  or or_5 (ALUop0, decoder_1_out0, decoder_1_out1, decoder_1_out2, decoder_1_out6, LWIRegWriteDataChoose, MemWriteEnable, BLEorBNE, SetOneForBLE);
  or or_6 (AddOrSub1, SetOneForBLE, decoder_1_out2, BLEorBNE);
  or or_7 (AreWeBranching, SetOneForBLE, BLEorBNE);
  or or_8 (ALUop2, decoder_1_out0, decoder_1_out1, decoder_1_out2, decoder_1_out4, LWIRegWriteDataChoose, MemWriteEnable, BLEorBNE, SetOneForBLE);
  or or_9 (SetOneForJ, JALReg7, decoder_1_out11);

  assign JALSTOREPCPLUSONE = JALReg7;
  assign ReadEnableKB = INPUTDATA1;
  assign SetOneForBNE = BLEorBNE;
endmodule

module leftbitshifter (
  input  [15:0] beforeshift,
  input  [2:0] shamt,
  output [15:0] aftershift
);

  wire multiplexer_1_out, multiplexer_2_out, multiplexer_3_out, multiplexer_4_out, multiplexer_5_out,
       multiplexer_6_out, multiplexer_7_out, multiplexer_8_out, multiplexer_9_out, multiplexer_10_out,
       multiplexer_11_out, multiplexer_12_out, multiplexer_13_out, multiplexer_14_out, multiplexer_15_out,
       multiplexer_16_out, multiplexer_17_out, multiplexer_18_out, multiplexer_19_out, multiplexer_20_out,
       multiplexer_21_out, multiplexer_22_out, multiplexer_23_out, multiplexer_24_out, multiplexer_25_out,
       multiplexer_26_out, multiplexer_27_out, multiplexer_28_out, multiplexer_29_out, multiplexer_30_out,
       multiplexer_31_out, multiplexer_32_out;

  Multiplexer #(.enable("false")) multiplexer_1 (
    .in0(beforeshift[15]), .in1(beforeshift[11]), .out(multiplexer_1_out), .sel(shamt[2]));
  Multiplexer #(.enable("false")) multiplexer_2 (
    .in0(beforeshift[14]), .in1(beforeshift[10]), .out(multiplexer_2_out), .sel(shamt[2]));
  Multiplexer #(.enable("false")) multiplexer_3 (
    .in0(beforeshift[13]), .in1(beforeshift[9]), .out(multiplexer_3_out), .sel(shamt[2]));
  Multiplexer #(.enable("false")) multiplexer_4 (
    .in0(beforeshift[12]), .in1(beforeshift[8]), .out(multiplexer_4_out), .sel(shamt[2]));
  Multiplexer #(.enable("false")) multiplexer_5 (
    .in0(beforeshift[11]), .in1(beforeshift[7]), .out(multiplexer_5_out), .sel(shamt[2]));
  Multiplexer #(.enable("false")) multiplexer_6 (
    .in0(beforeshift[10]), .in1(beforeshift[6]), .out(multiplexer_6_out), .sel(shamt[2]));
  Multiplexer #(.enable("false")) multiplexer_7 (
    .in0(beforeshift[9]), .in1(beforeshift[5]), .out(multiplexer_7_out), .sel(shamt[2]));
  Multiplexer #(.enable("false")) multiplexer_8 (
    .in0(beforeshift[8]), .in1(beforeshift[4]), .out(multiplexer_8_out), .sel(shamt[2]));
  Multiplexer #(.enable("false")) multiplexer_9 (
    .in0(beforeshift[7]), .in1(beforeshift[3]), .out(multiplexer_9_out), .sel(shamt[2]));
  Multiplexer #(.enable("false")) multiplexer_10 (
    .in0(beforeshift[6]), .in1(beforeshift[2]), .out(multiplexer_10_out), .sel(shamt[2]));
  Multiplexer #(.enable("false")) multiplexer_11 (
    .in0(beforeshift[5]), .in1(beforeshift[1]), .out(multiplexer_11_out), .sel(shamt[2]));
  Multiplexer #(.enable("false")) multiplexer_12 (
    .in0(beforeshift[4]), .in1(beforeshift[0]), .out(multiplexer_12_out), .sel(shamt[2]));
  Multiplexer #(.enable("false")) multiplexer_13 (
    .in0(beforeshift[3]), .in1(1'b0), .out(multiplexer_13_out), .sel(shamt[2]));
  Multiplexer #(.enable("false")) multiplexer_14 (
    .in0(beforeshift[2]), .in1(1'b0), .out(multiplexer_14_out), .sel(shamt[2]));
  Multiplexer #(.enable("false")) multiplexer_15 (
    .in0(beforeshift[1]), .in1(1'b0), .out(multiplexer_15_out), .sel(shamt[2]));
  Multiplexer #(.enable("false")) multiplexer_16 (
    .in0(beforeshift[0]), .in1(1'b0), .out(multiplexer_16_out), .sel(shamt[2]));
  Multiplexer #(.enable("false")) multiplexer_17 (
    .in0(multiplexer_1_out), .in1(multiplexer_3_out), .out(multiplexer_17_out), .sel(shamt[1]));
  Multiplexer #(.enable("false")) multiplexer_18 (
    .in0(multiplexer_2_out), .in1(multiplexer_4_out), .out(multiplexer_18_out), .sel(shamt[1]));
  Multiplexer #(.enable("false")) multiplexer_19 (
    .in0(multiplexer_3_out), .in1(multiplexer_5_out), .out(multiplexer_19_out), .sel(shamt[1]));
  Multiplexer #(.enable("false")) multiplexer_20 (
    .in0(multiplexer_4_out), .in1(multiplexer_6_out), .out(multiplexer_20_out), .sel(shamt[1]));
  Multiplexer #(.enable("false")) multiplexer_21 (
    .in0(multiplexer_5_out), .in1(multiplexer_7_out), .out(multiplexer_21_out), .sel(shamt[1]));
  Multiplexer #(.enable("false")) multiplexer_22 (
    .in0(multiplexer_6_out), .in1(multiplexer_8_out), .out(multiplexer_22_out), .sel(shamt[1]));
  Multiplexer #(.enable("false")) multiplexer_23 (
    .in0(multiplexer_7_out), .in1(multiplexer_9_out), .out(multiplexer_23_out), .sel(shamt[1]));
  Multiplexer #(.enable("false")) multiplexer_24 (
    .in0(multiplexer_8_out), .in1(multiplexer_10_out), .out(multiplexer_24_out), .sel(shamt[1]));
  Multiplexer #(.enable("false")) multiplexer_25 (
    .in0(multiplexer_9_out), .in1(multiplexer_11_out), .out(multiplexer_25_out), .sel(shamt[1]));
  Multiplexer #(.enable("false")) multiplexer_26 (
    .in0(multiplexer_10_out), .in1(multiplexer_12_out), .out(multiplexer_26_out), .sel(shamt[1]));
  Multiplexer #(.enable("false")) multiplexer_27 (
    .in0(multiplexer_11_out), .in1(multiplexer_13_out), .out(multiplexer_27_out), .sel(shamt[1]));
  Multiplexer #(.enable("false")) multiplexer_28 (
    .in0(multiplexer_12_out), .in1(multiplexer_14_out), .out(multiplexer_28_out), .sel(shamt[1]));
  Multiplexer #(.enable("false")) multiplexer_29 (
    .in0(multiplexer_13_out), .in1(multiplexer_15_out), .out(multiplexer_29_out), .sel(shamt[1]));
  Multiplexer #(.enable("false")) multiplexer_30 (
    .in0(multiplexer_14_out), .in1(multiplexer_16_out), .out(multiplexer_30_out), .sel(shamt[1]));
  Multiplexer #(.enable("false")) multiplexer_31 (
    .in0(multiplexer_15_out), .in1(1'b0), .out(multiplexer_31_out), .sel(shamt[1]));
  Multiplexer #(.enable("false")) multiplexer_32 (
    .in0(multiplexer_16_out), .in1(1'b0), .out(multiplexer_32_out), .sel(shamt[1]));
  Multiplexer #(.enable("false")) multiplexer_33 (
    .in0(multiplexer_17_out), .in1(multiplexer_18_out), .out(aftershift[15]), .sel(shamt[0]));
  Multiplexer #(.enable("false")) multiplexer_34 (
    .in0(multiplexer_18_out), .in1(multiplexer_19_out), .out(aftershift[14]), .sel(shamt[0]));
  Multiplexer #(.enable("false")) multiplexer_35 (
    .in0(multiplexer_19_out), .in1(multiplexer_20_out), .out(aftershift[13]), .sel(shamt[0]));
  Multiplexer #(.enable("false")) multiplexer_36 (
    .in0(multiplexer_20_out), .in1(multiplexer_21_out), .out(aftershift[12]), .sel(shamt[0]));
  Multiplexer #(.enable("false")) multiplexer_37 (
    .in0(multiplexer_21_out), .in1(multiplexer_22_out), .out(aftershift[11]), .sel(shamt[0]));
  Multiplexer #(.enable("false")) multiplexer_38 (
    .in0(multiplexer_22_out), .in1(multiplexer_23_out), .out(aftershift[10]), .sel(shamt[0]));
  Multiplexer #(.enable("false")) multiplexer_39 (
    .in0(multiplexer_23_out), .in1(multiplexer_24_out), .out(aftershift[9]), .sel(shamt[0]));
  Multiplexer #(.enable("false")) multiplexer_40 (
    .in0(multiplexer_24_out), .in1(multiplexer_25_out), .out(aftershift[8]), .sel(shamt[0]));
  Multiplexer #(.enable("false")) multiplexer_41 (
    .in0(multiplexer_25_out), .in1(multiplexer_26_out), .out(aftershift[7]), .sel(shamt[0]));
  Multiplexer #(.enable("false")) multiplexer_42 (
    .in0(multiplexer_26_out), .in1(multiplexer_27_out), .out(aftershift[6]), .sel(shamt[0]));
  Multiplexer #(.enable("false")) multiplexer_43 (
    .in0(multiplexer_27_out), .in1(multiplexer_28_out), .out(aftershift[5]), .sel(shamt[0]));
  Multiplexer #(.enable("false")) multiplexer_44 (
    .in0(multiplexer_28_out), .in1(multiplexer_29_out), .out(aftershift[4]), .sel(shamt[0]));
  Multiplexer #(.enable("false")) multiplexer_45 (
    .in0(multiplexer_29_out), .in1(multiplexer_30_out), .out(aftershift[3]), .sel(shamt[0]));
  Multiplexer #(.enable("false")) multiplexer_46 (
    .in0(multiplexer_30_out), .in1(multiplexer_31_out), .out(aftershift[2]), .sel(shamt[0]));
  Multiplexer #(.enable("false")) multiplexer_47 (
    .in0(multiplexer_31_out), .in1(multiplexer_32_out), .out(aftershift[1]), .sel(shamt[0]));
  Multiplexer #(.enable("false")) multiplexer_48 (
    .in0(multiplexer_32_out), .in1(1'b0), .out(aftershift[0]), .sel(shamt[0]));
endmodule

module rightbitshifter (
  input  [15:0] beforeshift,
  input  [2:0] shamt,
  output [15:0] aftershift
);

  wire multiplexer_1_out, multiplexer_2_out, multiplexer_3_out, multiplexer_4_out, multiplexer_5_out,
       multiplexer_6_out, multiplexer_7_out, multiplexer_8_out, multiplexer_9_out, multiplexer_10_out,
       multiplexer_11_out, multiplexer_12_out, multiplexer_13_out, multiplexer_14_out, multiplexer_15_out,
       multiplexer_16_out, multiplexer_17_out, multiplexer_18_out, multiplexer_19_out, multiplexer_20_out,
       multiplexer_21_out, multiplexer_22_out, multiplexer_23_out, multiplexer_24_out, multiplexer_25_out,
       multiplexer_26_out, multiplexer_27_out, multiplexer_28_out, multiplexer_29_out, multiplexer_30_out,
       multiplexer_31_out, multiplexer_32_out;

  Multiplexer #(.enable("false")) multiplexer_1 (
    .in0(beforeshift[15]), .in1(1'b0), .out(multiplexer_1_out), .sel(shamt[2]));
  Multiplexer #(.enable("false")) multiplexer_2 (
    .in0(beforeshift[14]), .in1(1'b0), .out(multiplexer_2_out), .sel(shamt[2]));
  Multiplexer #(.enable("false")) multiplexer_3 (
    .in0(beforeshift[13]), .in1(1'b0), .out(multiplexer_3_out), .sel(shamt[2]));
  Multiplexer #(.enable("false")) multiplexer_4 (
    .in0(beforeshift[12]), .in1(1'b0), .out(multiplexer_4_out), .sel(shamt[2]));
  Multiplexer #(.enable("false")) multiplexer_5 (
    .in0(beforeshift[11]), .in1(beforeshift[15]), .out(multiplexer_5_out), .sel(shamt[2]));
  Multiplexer #(.enable("false")) multiplexer_6 (
    .in0(beforeshift[10]), .in1(beforeshift[14]), .out(multiplexer_6_out), .sel(shamt[2]));
  Multiplexer #(.enable("false")) multiplexer_7 (
    .in0(beforeshift[9]), .in1(beforeshift[13]), .out(multiplexer_7_out), .sel(shamt[2]));
  Multiplexer #(.enable("false")) multiplexer_8 (
    .in0(beforeshift[8]), .in1(beforeshift[12]), .out(multiplexer_8_out), .sel(shamt[2]));
  Multiplexer #(.enable("false")) multiplexer_9 (
    .in0(beforeshift[7]), .in1(beforeshift[11]), .out(multiplexer_9_out), .sel(shamt[2]));
  Multiplexer #(.enable("false")) multiplexer_10 (
    .in0(beforeshift[6]), .in1(beforeshift[10]), .out(multiplexer_10_out), .sel(shamt[2]));
  Multiplexer #(.enable("false")) multiplexer_11 (
    .in0(beforeshift[5]), .in1(beforeshift[9]), .out(multiplexer_11_out), .sel(shamt[2]));
  Multiplexer #(.enable("false")) multiplexer_12 (
    .in0(beforeshift[4]), .in1(beforeshift[8]), .out(multiplexer_12_out), .sel(shamt[2]));
  Multiplexer #(.enable("false")) multiplexer_13 (
    .in0(beforeshift[3]), .in1(beforeshift[7]), .out(multiplexer_13_out), .sel(shamt[2]));
  Multiplexer #(.enable("false")) multiplexer_14 (
    .in0(beforeshift[2]), .in1(beforeshift[6]), .out(multiplexer_14_out), .sel(shamt[2]));
  Multiplexer #(.enable("false")) multiplexer_15 (
    .in0(beforeshift[1]), .in1(beforeshift[5]), .out(multiplexer_15_out), .sel(shamt[2]));
  Multiplexer #(.enable("false")) multiplexer_16 (
    .in0(beforeshift[0]), .in1(beforeshift[4]), .out(multiplexer_16_out), .sel(shamt[2]));
  Multiplexer #(.enable("false")) multiplexer_17 (
    .in0(multiplexer_1_out), .in1(1'b0), .out(multiplexer_17_out), .sel(shamt[1]));
  Multiplexer #(.enable("false")) multiplexer_18 (
    .in0(multiplexer_2_out), .in1(1'b0), .out(multiplexer_18_out), .sel(shamt[1]));
  Multiplexer #(.enable("false")) multiplexer_19 (
    .in0(multiplexer_3_out), .in1(multiplexer_1_out), .out(multiplexer_19_out), .sel(shamt[1]));
  Multiplexer #(.enable("false")) multiplexer_20 (
    .in0(multiplexer_4_out), .in1(multiplexer_2_out), .out(multiplexer_20_out), .sel(shamt[1]));
  Multiplexer #(.enable("false")) multiplexer_21 (
    .in0(multiplexer_5_out), .in1(multiplexer_3_out), .out(multiplexer_21_out), .sel(shamt[1]));
  Multiplexer #(.enable("false")) multiplexer_22 (
    .in0(multiplexer_6_out), .in1(multiplexer_4_out), .out(multiplexer_22_out), .sel(shamt[1]));
  Multiplexer #(.enable("false")) multiplexer_23 (
    .in0(multiplexer_7_out), .in1(multiplexer_5_out), .out(multiplexer_23_out), .sel(shamt[1]));
  Multiplexer #(.enable("false")) multiplexer_24 (
    .in0(multiplexer_8_out), .in1(multiplexer_6_out), .out(multiplexer_24_out), .sel(shamt[1]));
  Multiplexer #(.enable("false")) multiplexer_25 (
    .in0(multiplexer_9_out), .in1(multiplexer_7_out), .out(multiplexer_25_out), .sel(shamt[1]));
  Multiplexer #(.enable("false")) multiplexer_26 (
    .in0(multiplexer_10_out), .in1(multiplexer_8_out), .out(multiplexer_26_out), .sel(shamt[1]));
  Multiplexer #(.enable("false")) multiplexer_27 (
    .in0(multiplexer_11_out), .in1(multiplexer_9_out), .out(multiplexer_27_out), .sel(shamt[1]));
  Multiplexer #(.enable("false")) multiplexer_28 (
    .in0(multiplexer_12_out), .in1(multiplexer_10_out), .out(multiplexer_28_out), .sel(shamt[1]));
  Multiplexer #(.enable("false")) multiplexer_29 (
    .in0(multiplexer_13_out), .in1(multiplexer_11_out), .out(multiplexer_29_out), .sel(shamt[1]));
  Multiplexer #(.enable("false")) multiplexer_30 (
    .in0(multiplexer_14_out), .in1(multiplexer_12_out), .out(multiplexer_30_out), .sel(shamt[1]));
  Multiplexer #(.enable("false")) multiplexer_31 (
    .in0(multiplexer_15_out), .in1(multiplexer_13_out), .out(multiplexer_31_out), .sel(shamt[1]));
  Multiplexer #(.enable("false")) multiplexer_32 (
    .in0(multiplexer_16_out), .in1(multiplexer_14_out), .out(multiplexer_32_out), .sel(shamt[1]));
  Multiplexer #(.enable("false")) multiplexer_33 (
    .in0(multiplexer_17_out), .in1(1'b0), .out(aftershift[15]), .sel(shamt[0]));
  Multiplexer #(.enable("false")) multiplexer_34 (
    .in0(multiplexer_18_out), .in1(multiplexer_17_out), .out(aftershift[14]), .sel(shamt[0]));
  Multiplexer #(.enable("false")) multiplexer_35 (
    .in0(multiplexer_19_out), .in1(multiplexer_18_out), .out(aftershift[13]), .sel(shamt[0]));
  Multiplexer #(.enable("false")) multiplexer_36 (
    .in0(multiplexer_20_out), .in1(multiplexer_19_out), .out(aftershift[12]), .sel(shamt[0]));
  Multiplexer #(.enable("false")) multiplexer_37 (
    .in0(multiplexer_21_out), .in1(multiplexer_20_out), .out(aftershift[11]), .sel(shamt[0]));
  Multiplexer #(.enable("false")) multiplexer_38 (
    .in0(multiplexer_22_out), .in1(multiplexer_21_out), .out(aftershift[10]), .sel(shamt[0]));
  Multiplexer #(.enable("false")) multiplexer_39 (
    .in0(multiplexer_23_out), .in1(multiplexer_22_out), .out(aftershift[9]), .sel(shamt[0]));
  Multiplexer #(.enable("false")) multiplexer_40 (
    .in0(multiplexer_24_out), .in1(multiplexer_23_out), .out(aftershift[8]), .sel(shamt[0]));
  Multiplexer #(.enable("false")) multiplexer_41 (
    .in0(multiplexer_25_out), .in1(multiplexer_24_out), .out(aftershift[7]), .sel(shamt[0]));
  Multiplexer #(.enable("false")) multiplexer_42 (
    .in0(multiplexer_26_out), .in1(multiplexer_25_out), .out(aftershift[6]), .sel(shamt[0]));
  Multiplexer #(.enable("false")) multiplexer_43 (
    .in0(multiplexer_27_out), .in1(multiplexer_26_out), .out(aftershift[5]), .sel(shamt[0]));
  Multiplexer #(.enable("false")) multiplexer_44 (
    .in0(multiplexer_28_out), .in1(multiplexer_27_out), .out(aftershift[4]), .sel(shamt[0]));
  Multiplexer #(.enable("false")) multiplexer_45 (
    .in0(multiplexer_29_out), .in1(multiplexer_28_out), .out(aftershift[3]), .sel(shamt[0]));
  Multiplexer #(.enable("false")) multiplexer_46 (
    .in0(multiplexer_30_out), .in1(multiplexer_29_out), .out(aftershift[2]), .sel(shamt[0]));
  Multiplexer #(.enable("false")) multiplexer_47 (
    .in0(multiplexer_31_out), .in1(multiplexer_30_out), .out(aftershift[1]), .sel(shamt[0]));
  Multiplexer #(.enable("false")) multiplexer_48 (
    .in0(multiplexer_32_out), .in1(multiplexer_31_out), .out(aftershift[0]), .sel(shamt[0]));
endmodule

module memory_latch (
  input  [15:0] address,
  input  WE,
  input  clk,
  input  [15:0] data_in,
  output [15:0] address_latched,
  output WE_latched,
  output OE_latched,
  output [15:0] data_in_latched
);

  wire DMwe_latch_q;
  wire [15:0] addr_latch_q;

  Register #(.width(16), .trigger("falling")) addr_latch (
    .D(address), .en(WE), .clk(clk), .Q(addr_latch_q));  // open: clr
  D_Flip_Flop #(.trigger("falling")) DMwe_latch (.D(WE), .clk(clk), .Q(DMwe_latch_q));  // open: Qn, preset, reset
  Register #(.width(16), .trigger("falling")) data_to_be_written (
    .D(data_in), .en(WE), .clk(clk), .Q(data_in_latched));  // open: clr
  Multiplexer #(.width(16), .enable("false")) multiplexer_1 (
    .in0(address), .in1(addr_latch_q), .out(address_latched), .sel(DMwe_latch_q));
  and and_1 (WE_latched, clk, DMwe_latch_q);
  not not_1 (OE_latched, WE_latched);
endmodule
